# Fritzing sketch USB Keystroke Injector (saved by Fritzing 0.9.3b)
breadboards: 1

parts:
  Pro_Micro1 = Pro Micro
  Part1 = Bluetooth HC-05 Macho
  R2 = Resistor [tolerance=±5% resistance=1k package=THT]
  R3 = Resistor [tolerance=±5% resistance=1k package=THT]
  R1 = Resistor [tolerance=±5% resistance=1k package=THT]
  Part2 = MicroSD Card Module
  S1 = Pushbutton [package=THT]
  S2 = Pushbutton [package=THT]
  S3 = Pushbutton [package=THT]
  S4 = Pushbutton [package=THT]
  S5 = Pushbutton [package=THT]
  S6 = Pushbutton [package=THT]
  LED1 = LED - 5mm [color="Yellow (585nm)" package="5 mm [THT]"]
  R4 = Resistor [tolerance=±5% resistance=2.2k package=THT]
  R6 = Resistor [tolerance=±5% resistance=10k package=THT]
  R5 = Photocell (LDR) [package=THT]

nets:
  N1: Pro_Micro1.TX1, R1.Pin_1
  N2: Pro_Micro1.RX0, Part1.TXD
  N3: Pro_Micro1.D2, S6.leg1
  N4: Pro_Micro1.D3, S1.leg1
  N5: Pro_Micro1.D4, S2.leg1
  N6: Pro_Micro1.D5, S3.leg1
  N7: Pro_Micro1.D6, S4.leg1
  N8: Pro_Micro1.D7, S5.leg1
  N9: Pro_Micro1.D8, Part1.State
  N10: Pro_Micro1.D10, Part2.CS
  N11: Pro_Micro1.D16/MOSI, Part2.MOSI
  N12: Pro_Micro1.D14/MISO, Part2.MISO
  N13: Pro_Micro1.D15/SCLK, Part2.SCK
  N14: Pro_Micro1.D20/A2, R6.Pin_0, R5.pin_0
  N15: Pro_Micro1.D21/A3, R4.Pin_1
  VCC: Pro_Micro1.VCC, Part1.VCC, Part2.VCC, R5.pin_1
  GND: Pro_Micro1.GND, Part1.GND, R2.Pin_0, R2.Pin_1, R3.Pin_1, Part2.GND, S1.leg0, S2.leg0, S3.leg0, S4.leg0, S5.leg0, S6.leg0, LED1.cathode, R6.Pin_1
  N16: Part1.RXD, R3.Pin_0, R1.Pin_0
  N17: LED1.anode, R4.Pin_0

custom parts:
  Pro Micro: The SparkFun Pro Micro is a complete USB-based microcontoller development system, in a very small footprint, capable of implementing many types of projects. All programming can be done via the USB port.
